// Logisim project DDCA PROJECT FINAL 2.circ as structural Verilog: 1 circuit, main circuit main
module main (
  input  [7:0] INPUT,
  output SIGN,
  output [6:0] MAGNITUDE
);


  assign MAGNITUDE = INPUT[6:0];
  assign SIGN = INPUT[7];

  // Notes on the sheet:
  //   INPUT EXAMPLE: +45
  //   SPLITTER
endmodule
